// Digital circuit 4-bit-Processor.dig as structural Verilog
module _4_bit_Processor (
  input  [1:0] IR_ctrl,
  input  [1:0] Mem_ctrl,
  input  [3:0] Mem_input,
  input  clk,
  input  [1:0] PC_ctrl,
  output [15:0] Instr_16bit,
  output [3:0] PC_output,
  output [3:0] Read_data_1,
  output [3:0] Read_data_2,
  output [3:0] ALU_output
);

  wire instruction_memory_module_1_alu_enable;
  wire [7:0] multiplexer_1_out, registerfile_write_control_1_write_ctrl;

  Instruction_Memory_Module instruction_memory_module_1 (
    .IR_ctrl(IR_ctrl), .PC_ctrl(PC_ctrl), .Instruction_MemCtrl(Mem_ctrl), .Instruction_MemInput(Mem_input),
    .clk(clk), .IR_output(Instr_16bit), .PC_output(PC_output),
    .ALU_enable(instruction_memory_module_1_alu_enable));
  RegisterFile_Write_Control registerfile_write_control_1 (
    .OpCode_3(Instr_16bit[1:0]), .Write_ctrl(registerfile_write_control_1_write_ctrl));
  Multiplexer #(.Bits(8)) multiplexer_1 (
    .sel(instruction_memory_module_1_alu_enable), .in_0({8{1'b0}}),
    .in_1(registerfile_write_control_1_write_ctrl), .out(multiplexer_1_out));
  Register_File register_file_1 (
    .Select_Read1(Instr_16bit[5:4]), .Select_Read2(Instr_16bit[3:2]), .Write_Data(ALU_output),
    .Select_Write(Instr_16bit[1:0]), .Ctrl_Registers(multiplexer_1_out), .clk(clk),
    .Read_Data_1(Read_data_1), .Read_Data_2(Read_data_2));
  Arithmetic_Logic_Unit_ALU arithmetic_logic_unit_alu_1 (
    .A(Read_data_1), .B(Read_data_2), .S_1_S_0_C_in(Instr_16bit[8:6]), .D(ALU_output));  // open: Overflow

  // Notes on the sheet:
  //   PC_ctrl: default 1
endmodule

/* Test case testing:
clk IR_ctrl Mem_ctrl Mem_input PC_ctrl PC_output Instr_16bit Read-data_1 Read-data_2 ALU_output
c 0 1 0x0 1 x x x x x
c 0 1 0x4 1 x x x x x
c 0 1 0x1 1 x x x x x
c 0 1 0x0 1 x x x x x

c 0 1 0x0 1 x x x x x
c 0 1 0x4 1 x x x x x
c 0 1 0x1 1 x x x x x
c 0 1 0x0 1 x x x x x

c 0 1 0x1 1 x x x x x
c 0 1 0x5 1 x x x x x
c 0 1 0x1 1 x x x x x
c 0 1 0x0 1 x x x x x

c 0 1 0x6 1 x x x x x
c 0 1 0x0 1 x x x x x
c 0 1 0x0 1 x x x x x
c 0 1 0x0 1 x x x x x


c 1 0 2 1 x x x x x
c 1 0 2 1 x x x x x
c 1 0 2 1 x x x x x
c 1 0 2 1 x x x x x
c 1 0 2 1 x x x x x
c 1 0 2 1 x x x x x
c 1 0 2 1 x x x x x
c 1 0 2 1 x x x x x
c 1 0 2 1 x x x x x
c 1 0 2 1 x x x x x
c 1 0 1 1 x x x x x
c 1 0 1 1 x x x x x
c 1 0 1 1 x x x x x
c 1 0 1 1 x x x x x
c 1 0 1 1 x x x x x
c 1 0 1 1 x x x x x
*/
