// Digital circuit Arithmetic Logic Unit(ALU).dig as structural Verilog
module Arithmetic_Logic_Unit_ALU (
  input  [3:0] A,
  input  [3:0] B,
  input  [2:0] S_1_S_0_C_in,
  output [3:0] D,
  output Overflow
);

  wire [3:0] multiplexer_1_out, not_1_out, not_2_out;

  assign not_1_out = ~B;  // Not not_1, 4 bits wide
  assign not_2_out = ~4'b0000;  // Not not_2, 4 bits wide
  Multiplexer #(.Selector_Bits(2), .Bits(4)) multiplexer_1 (
    .sel(S_1_S_0_C_in[2:1]), .in_0(B), .in_1(not_1_out), .in_2(4'b0000), .in_3(not_2_out),
    .out(multiplexer_1_out));
  _4_bit_adder_modified _4_bit_adder_modified_1 (
    .A(A), .B(multiplexer_1_out), .C_in(S_1_S_0_C_in[0]), .Sum(D), .Overflow_Flag(Overflow));
endmodule
