// Digital circuit GPR.dig as structural Verilog
module GPR (
  input  [1:0] Control,
  input  [3:0] Input,
  input  Clock,
  input  [3:0] Address,
  output [3:0] Output
);

  wire and_1_out, and_2_out, and_3_out, and_4_out, and_5_out, and_6_out, and_7_out, and_8_out, and_9_out,
       and_10_out, and_11_out, and_12_out, and_13_out, and_14_out, and_15_out, and_16_out, decoder_1_out_0,
       decoder_1_out_1, decoder_1_out_2, decoder_1_out_3, decoder_1_out_4, decoder_1_out_5, decoder_1_out_6,
       decoder_1_out_7, decoder_1_out_8, decoder_1_out_9, decoder_1_out_10, decoder_1_out_11,
       decoder_1_out_12, decoder_1_out_13, decoder_1_out_14, decoder_1_out_15;
  wire [3:0] fourbitinstructionregister_1_output, fourbitinstructionregister_2_output,
       fourbitinstructionregister_3_output, fourbitinstructionregister_4_output,
       fourbitinstructionregister_5_output, fourbitinstructionregister_6_output,
       fourbitinstructionregister_7_output, fourbitinstructionregister_8_output,
       fourbitinstructionregister_9_output, fourbitinstructionregister_10_output,
       fourbitinstructionregister_11_output, fourbitinstructionregister_12_output,
       fourbitinstructionregister_13_output, fourbitinstructionregister_14_output,
       fourbitinstructionregister_15_output, fourbitinstructionregister_16_output;

  Decoder #(.Selector_Bits(4)) decoder_1 (
    .sel(Address), .out_0(decoder_1_out_0), .out_1(decoder_1_out_1), .out_2(decoder_1_out_2),
    .out_3(decoder_1_out_3), .out_4(decoder_1_out_4), .out_5(decoder_1_out_5), .out_6(decoder_1_out_6),
    .out_7(decoder_1_out_7), .out_8(decoder_1_out_8), .out_9(decoder_1_out_9), .out_10(decoder_1_out_10),
    .out_11(decoder_1_out_11), .out_12(decoder_1_out_12), .out_13(decoder_1_out_13),
    .out_14(decoder_1_out_14), .out_15(decoder_1_out_15));
  and and_1 (and_1_out, Clock, decoder_1_out_0);
  and and_2 (and_2_out, Clock, decoder_1_out_1);
  and and_3 (and_3_out, Clock, decoder_1_out_2);
  and and_4 (and_4_out, Clock, decoder_1_out_3);
  and and_5 (and_5_out, Clock, decoder_1_out_4);
  and and_6 (and_6_out, Clock, decoder_1_out_5);
  and and_7 (and_7_out, Clock, decoder_1_out_6);
  and and_8 (and_8_out, Clock, decoder_1_out_7);
  and and_9 (and_9_out, Clock, decoder_1_out_8);
  and and_10 (and_10_out, Clock, decoder_1_out_9);
  and and_11 (and_11_out, Clock, decoder_1_out_10);
  and and_12 (and_12_out, Clock, decoder_1_out_11);
  and and_13 (and_13_out, Clock, decoder_1_out_12);
  and and_14 (and_14_out, Clock, decoder_1_out_13);
  and and_15 (and_15_out, Clock, decoder_1_out_14);
  and and_16 (and_16_out, Clock, decoder_1_out_15);
  FourBitInstructionRegister fourbitinstructionregister_1 (
    .Clock(and_1_out), .Control(Control), .Input(Input), .Output(fourbitinstructionregister_1_output));
  FourBitInstructionRegister fourbitinstructionregister_2 (
    .Clock(and_2_out), .Control(Control), .Input(Input), .Output(fourbitinstructionregister_2_output));
  FourBitInstructionRegister fourbitinstructionregister_3 (
    .Clock(and_3_out), .Control(Control), .Input(Input), .Output(fourbitinstructionregister_3_output));
  FourBitInstructionRegister fourbitinstructionregister_4 (
    .Clock(and_4_out), .Control(Control), .Input(Input), .Output(fourbitinstructionregister_4_output));
  FourBitInstructionRegister fourbitinstructionregister_5 (
    .Clock(and_5_out), .Control(Control), .Input(Input), .Output(fourbitinstructionregister_5_output));
  FourBitInstructionRegister fourbitinstructionregister_6 (
    .Clock(and_6_out), .Control(Control), .Input(Input), .Output(fourbitinstructionregister_6_output));
  FourBitInstructionRegister fourbitinstructionregister_7 (
    .Clock(and_7_out), .Control(Control), .Input(Input), .Output(fourbitinstructionregister_7_output));
  FourBitInstructionRegister fourbitinstructionregister_8 (
    .Clock(and_8_out), .Control(Control), .Input(Input), .Output(fourbitinstructionregister_8_output));
  FourBitInstructionRegister fourbitinstructionregister_9 (
    .Clock(and_9_out), .Control(Control), .Input(Input), .Output(fourbitinstructionregister_9_output));
  FourBitInstructionRegister fourbitinstructionregister_10 (
    .Clock(and_10_out), .Control(Control), .Input(Input), .Output(fourbitinstructionregister_10_output));
  FourBitInstructionRegister fourbitinstructionregister_11 (
    .Clock(and_11_out), .Control(Control), .Input(Input), .Output(fourbitinstructionregister_11_output));
  FourBitInstructionRegister fourbitinstructionregister_12 (
    .Clock(and_12_out), .Control(Control), .Input(Input), .Output(fourbitinstructionregister_12_output));
  FourBitInstructionRegister fourbitinstructionregister_13 (
    .Clock(and_13_out), .Control(Control), .Input(Input), .Output(fourbitinstructionregister_13_output));
  FourBitInstructionRegister fourbitinstructionregister_14 (
    .Clock(and_14_out), .Control(Control), .Input(Input), .Output(fourbitinstructionregister_14_output));
  FourBitInstructionRegister fourbitinstructionregister_15 (
    .Clock(and_15_out), .Control(Control), .Input(Input), .Output(fourbitinstructionregister_15_output));
  FourBitInstructionRegister fourbitinstructionregister_16 (
    .Clock(and_16_out), .Control(Control), .Input(Input), .Output(fourbitinstructionregister_16_output));
  Multiplexer #(.Selector_Bits(4), .Bits(4)) multiplexer_1 (
    .sel(Address), .in_0(fourbitinstructionregister_1_output), .in_1(fourbitinstructionregister_2_output),
    .in_2(fourbitinstructionregister_3_output), .in_3(fourbitinstructionregister_4_output),
    .in_4(fourbitinstructionregister_5_output), .in_5(fourbitinstructionregister_6_output),
    .in_6(fourbitinstructionregister_7_output), .in_7(fourbitinstructionregister_8_output),
    .in_8(fourbitinstructionregister_9_output), .in_9(fourbitinstructionregister_10_output),
    .in_10(fourbitinstructionregister_11_output), .in_11(fourbitinstructionregister_12_output),
    .in_12(fourbitinstructionregister_13_output), .in_13(fourbitinstructionregister_14_output),
    .in_14(fourbitinstructionregister_15_output), .in_15(fourbitinstructionregister_16_output), .out(Output));
endmodule
