// Digital circuit Instruction-Memory-Module.dig as structural Verilog
module Instruction_Memory_Module (
  input  [1:0] IR_ctrl,
  input  [1:0] PC_ctrl,
  input  [1:0] Instruction_MemCtrl,
  input  [3:0] Instruction_MemInput,
  input  clk,
  output [15:0] IR_output,
  output [3:0] PC_output,
  output ALU_enable
);

  wire not_1_out, not_2_out;
  wire [1:0] demultiplexer_1_out_0, demultiplexer_1_out_1, demultiplexer_1_out_2, demultiplexer_1_out_3;
  wire [3:0] demultiplexer_2_out_0, demultiplexer_2_out_1, demultiplexer_2_out_2, demultiplexer_2_out_3,
       fourbitinstructionregister_1_output, fourbitinstructionregister_2_output,
       fourbitinstructionregister_3_output, fourbitinstructionregister_4_output, gpr_1_output;

  _4_bit_ProgramCounter _4_bit_programcounter_1 (.clk(clk), .Control(PC_ctrl), .Output(PC_output));
  GPR gpr_1 (
    .Control(Instruction_MemCtrl), .Input(Instruction_MemInput), .Clock(clk), .Address(PC_output),
    .Output(gpr_1_output));
  Demultiplexer #(.Selector_Bits(2), .Bits(2)) demultiplexer_1 (
    .sel(PC_output[1:0]), .in(IR_ctrl), .out_0(demultiplexer_1_out_0), .out_1(demultiplexer_1_out_1),
    .out_2(demultiplexer_1_out_2), .out_3(demultiplexer_1_out_3));
  Demultiplexer #(.Selector_Bits(2), .Bits(4)) demultiplexer_2 (
    .sel(PC_output[1:0]), .in(gpr_1_output), .out_0(demultiplexer_2_out_0), .out_1(demultiplexer_2_out_1),
    .out_2(demultiplexer_2_out_2), .out_3(demultiplexer_2_out_3));
  not not_1 (not_1_out, PC_output[0]);
  not not_2 (not_2_out, PC_output[1]);
  FourBitInstructionRegister fourbitinstructionregister_1 (
    .Clock(clk), .Control(demultiplexer_1_out_0), .Input(demultiplexer_2_out_0),
    .Output(fourbitinstructionregister_1_output));
  FourBitInstructionRegister fourbitinstructionregister_2 (
    .Clock(clk), .Control(demultiplexer_1_out_1), .Input(demultiplexer_2_out_1),
    .Output(fourbitinstructionregister_2_output));
  FourBitInstructionRegister fourbitinstructionregister_3 (
    .Clock(clk), .Control(demultiplexer_1_out_2), .Input(demultiplexer_2_out_2),
    .Output(fourbitinstructionregister_3_output));
  FourBitInstructionRegister fourbitinstructionregister_4 (
    .Clock(clk), .Control(demultiplexer_1_out_3), .Input(demultiplexer_2_out_3),
    .Output(fourbitinstructionregister_4_output));
  and and_1 (ALU_enable, not_1_out, not_2_out);
  assign IR_output = ALU_enable ? {fourbitinstructionregister_4_output, fourbitinstructionregister_3_output, fourbitinstructionregister_2_output, fourbitinstructionregister_1_output} : 16'bz;  // Driver driver_1

  // Notes on the sheet:
  //   PC_ctrl: default 1
endmodule
