// Digital circuit Register-File.dig as structural Verilog
module Register_File (
  input  [1:0] Select_Read1,
  input  [1:0] Select_Read2,
  input  [3:0] Write_Data,
  input  [1:0] Select_Write,
  input  [7:0] Ctrl_Registers,
  input  clk,
  output [3:0] Read_Data_1,
  output [3:0] Read_Data_2
);

  wire [3:0] demultiplexer_1_out_0, demultiplexer_1_out_1, demultiplexer_1_out_2, demultiplexer_1_out_3,
       R_0_output, R_1_output, R_2_output, R_3_output;

  Demultiplexer #(.Selector_Bits(2), .Bits(4)) demultiplexer_1 (
    .sel(Select_Write), .in(Write_Data), .out_0(demultiplexer_1_out_0), .out_1(demultiplexer_1_out_1),
    .out_2(demultiplexer_1_out_2), .out_3(demultiplexer_1_out_3));
  FourBitInstructionRegister R_0 (
    .Clock(clk), .Control(Ctrl_Registers[1:0]), .Input(demultiplexer_1_out_0), .Output(R_0_output));
  FourBitInstructionRegister R_1 (
    .Clock(clk), .Control(Ctrl_Registers[3:2]), .Input(demultiplexer_1_out_1), .Output(R_1_output));
  FourBitInstructionRegister R_2 (
    .Clock(clk), .Control(Ctrl_Registers[5:4]), .Input(demultiplexer_1_out_2), .Output(R_2_output));
  FourBitInstructionRegister R_3 (
    .Clock(clk), .Control(Ctrl_Registers[7:6]), .Input(demultiplexer_1_out_3), .Output(R_3_output));
  Multiplexer #(.Selector_Bits(2), .Bits(4)) multiplexer_1 (
    .sel(Select_Read1), .in_0(R_0_output), .in_1(R_1_output), .in_2(R_2_output), .in_3(R_3_output),
    .out(Read_Data_1));
  Multiplexer #(.Selector_Bits(2), .Bits(4)) multiplexer_2 (
    .sel(Select_Read2), .in_0(R_0_output), .in_1(R_1_output), .in_2(R_2_output), .in_3(R_3_output),
    .out(Read_Data_2));
endmodule
