// Digital circuit RegisterFile-Write-Control.dig as structural Verilog
module RegisterFile_Write_Control (
  input  [1:0] OpCode_3,
  output [7:0] Write_ctrl
);

  Decoder #(.Selector_Bits(2)) decoder_1 (
    .sel(OpCode_3), .out_0(Write_ctrl[0]), .out_1(Write_ctrl[2]), .out_2(Write_ctrl[4]), .out_3(Write_ctrl[6]));

  assign {Write_ctrl[7], Write_ctrl[5], Write_ctrl[3], Write_ctrl[1]} = 4'b0000;
endmodule
