// Digital circuit intr-mem-module.dig as structural Verilog
module intr_mem_module (
  input  clk,
  input  [1:0] IR_ctrl,
  input  [1:0] pc_ctrl,
  input  [1:0] intr_mem_ctrl,
  input  [3:0] instr_mem_input,
  output [15:0] ir_output,
  output [3:0] pc_output,
  output ALU_Enable
);

  wire [1:0] demultiplexer_1_out_0, demultiplexer_1_out_1, demultiplexer_1_out_2, demultiplexer_1_out_3;
  wire [3:0] demultiplexer_2_out_0, demultiplexer_2_out_1, demultiplexer_2_out_2, demultiplexer_2_out_3,
       fourbitinstructionregister_1_output, fourbitinstructionregister_2_output,
       fourbitinstructionregister_3_output, gpr_1_output, R_0_output;

  // _4_bit_ProgramCounter__1 _4_bit_programcounter__1_1: pin names not known; wires that end beside it: clk, pc_ctrl, pc_output
  GPR gpr_1 (.Control(intr_mem_ctrl), .Input(instr_mem_input), .Clock(clk), .Address(pc_output), .Output(gpr_1_output));
  Demultiplexer #(.Selector_Bits(2), .Bits(2)) demultiplexer_1 (
    .sel(pc_output[1:0]), .in(IR_ctrl), .out_0(demultiplexer_1_out_0), .out_1(demultiplexer_1_out_1),
    .out_2(demultiplexer_1_out_2), .out_3(demultiplexer_1_out_3));
  Demultiplexer #(.Selector_Bits(2), .Bits(4)) demultiplexer_2 (
    .sel(pc_output[1:0]), .in(gpr_1_output), .out_0(demultiplexer_2_out_0), .out_1(demultiplexer_2_out_1),
    .out_2(demultiplexer_2_out_2), .out_3(demultiplexer_2_out_3));
  FourBitInstructionRegister R_0 (
    .Clock(clk), .Control(demultiplexer_1_out_0), .Input(demultiplexer_2_out_0), .Output(R_0_output));
  FourBitInstructionRegister fourbitinstructionregister_1 (
    .Clock(clk), .Control(demultiplexer_1_out_1), .Input(demultiplexer_2_out_1),
    .Output(fourbitinstructionregister_1_output));
  FourBitInstructionRegister fourbitinstructionregister_2 (
    .Clock(clk), .Control(demultiplexer_1_out_2), .Input(demultiplexer_2_out_2),
    .Output(fourbitinstructionregister_2_output));
  FourBitInstructionRegister fourbitinstructionregister_3 (
    .Clock(clk), .Control(demultiplexer_1_out_3), .Input(demultiplexer_2_out_3),
    .Output(fourbitinstructionregister_3_output));
  and and_1 (ALU_Enable, ~pc_output[0], ~pc_output[1]);  // And
  assign ir_output = ALU_Enable ? {fourbitinstructionregister_3_output, fourbitinstructionregister_2_output, fourbitinstructionregister_1_output, R_0_output} : 16'bz;  // Driver driver_1

  // Notes on the sheet:
  //   pc_ctrl: default 1
endmodule

/* Test case Test:
IR-ctrl intr-mem-ctrl instr-mem-input pc-ctrl clk pc-output ir-output ALU-Enable
0 1 0 1 C x x x
0 1 1 1 C x x x
0 1 2 1 C x x x
0 1 3 1 C x x x
0 1 4 1 C x x x
0 1 5 1 C x x x
0 1 6 1 C x x x
0 1 7 1 C x x x
0 1 8 1 C x x x
0 1 9 1 C x x x
0 1 10 1 C x x x 
0 1 11 1 C x x x 
0 1 12 1 C x x x
0 1 13 1 C x x x
0 1 14 1 C x x x
0 1 15 1 C x x x
1 0 0 1 C x x x
1 0 0 1 C x x x
1 0 0 1 C x x x
1 0 0 1 C x x x
1 0 0 1 C x x x
1 0 0 1 C x x x
1 0 0 1 C x x x
1 0 0 1 C x x x
1 0 0 1 C x x x
1 0 0 1 C x x x
1 0 0 1 C x x x
1 0 0 1 C x x x
1 0 0 1 C x x x
1 0 0 1 C x x x
1 0 0 1 C x x x 
1 0 0 1 C x x x
1 0 0 1 C x x x
1 0 0 1 C x x x
1 0 0 1 C x x x
*/
